# Fritzing sketch ESP8266Recognizer (saved by Fritzing 0.9.2b)
breadboards: 1
perfboards: 1

parts:
  R1 = Resistor [tolerance=±5% resistance=51 package=THT]
  C1 = Ceramic Capacitor [capacitance=100nF package="100 mil [THT, multilayer]"]
  R2 = Resistor [tolerance=±5% resistance=51 package=THT]
  C2 = Ceramic Capacitor [capacitance=100nF package="100 mil [THT, multilayer]"]
  U1 = ESP-WROOM-02-AE [part_number=ESP-WROOM-02-AE]
  R3 = Resistor [tolerance=±5% resistance=1.5k package=THT]
  R4 = Resistor [tolerance=±5% resistance=330 package=THT]
  R5 = Resistor [tolerance=±5% resistance=10k package=THT]
  R6 = Resistor [tolerance=±5% resistance=10k package=THT]
  LED1 = LED - 5mm [color="Red (633nm)" package="5 mm [THT]"]
  S2 = Pushbutton [package=THT]
  V5 = DC Power [voltage=3.3V]
  S1 = Pushbutton [package=THT]
  C3 = Ceramic Capacitor [capacitance=100nF package="100 mil [THT, multilayer]"]

nets:
  VCC: R1.Pin_0, C1.1
  N1: R1.Pin_1, R2.Pin_0, C2.1
  GND: C1.0, C2.0, U1.IO15, U1.GND, R4.Pin_1, LED1.cathode, S2.leg1, V5.V-, S1.leg0
  3.3V: R2.Pin_1, U1.3V3, R3.Pin_0, R5.Pin_0, R6.Pin_0, V5.V+
  N2: U1.EN, R5.Pin_1
  N3: U1.IO13, LED1.anode
  N4: U1.IO2, R6.Pin_1
  N5: U1.IO0, S1.leg1
  TOUT: U1.TOUT, R3.Pin_1, R4.Pin_0, C3.1
  N6: U1.RST, S2.leg0
  RX: U1.TXD
  TX: U1.RXD
  OUT: C3.0

custom parts:
  ESP-WROOM-02-AE: ESP-WROOM-02 with the DIP breakout board by Akizuki-Electronics in Japan. See http://akizukidenshi.com/catalog/g/gK-09758/ for the detauls.
